// Logisim project q1lab5.circ as structural Verilog: 1 circuit, main circuit main
module main (
  input  X0,
  input  Y0,
  input  C0,
  input  X1,
  input  Y1,
  input  in_6,
  input  X2,
  input  Y2,
  input  X3,
  input  Y3
);

  wire and_1_out, and_2_out, and_3_out, and_4_out, C1_out, C2_out, C3_out, G0_out, G1_out, G2_out, G3_out,
       P0_out, P1_out, P1G0_out, P1P0C0_out, P2_out, P2G1_out, P2P1G0_out, P2P1P0C0_out, P3_out, P3P2G1_out,
       S3_out;
  wire [0:0] C4_out;
  wire [3:0] S0_out;

  and G0 (G0_out, Y0, X0);
  and G1 (G1_out, Y1, X1);
  and G3 (G3_out, Y3, X3);
  xor P0 (P0_out, X0, Y0);
  xor P1 (P1_out, X1, Y1);
  xor P2 (P2_out, X2, Y2);
  xor P3 (P3_out, X3, Y3);
  and P1G0 (P1G0_out, P1_out, G0_out);
  and P2P1P0C0 (P2P1P0C0_out, P2_out, P1P0C0_out);
  and P2P1G0 (P2P1G0_out, P2_out, P1G0_out);
  xor S0 (S0_out[0], P0_out, C0);
  and and_1 (and_1_out, P0_out, C0);
  xor S0_2 (S0_out[1], P1_out, C1_out);
  and P1P0C0 (P1P0C0_out, P1_out, P0_out, C0);
  xor S2 (S0_out[2], P2_out, C2_out);
  and P2G1 (P2G1_out, G1_out, P2_out);
  and G2 (G2_out, X2, Y2);
  and P3P2G1 (P3P2G1_out, P2G1_out, P3_out);
  and and_2 (and_2_out, P2P1G0_out, P3_out);
  and and_3 (and_3_out, P2P1P0C0_out, P3_out);
  and and_4 (and_4_out, G2_out, P3_out);
  or C3 (C3_out, P2P1P0C0_out, P2P1G0_out, P2G1_out, G2_out);
  xor S3 (S3_out, P3_out, C3_out);
  or C1 (C1_out, and_1_out, G0_out);
  or C2 (C2_out, P1P0C0_out, P1G0_out, G1_out);
  or C4 (C4_out[0], P3P2G1_out, and_2_out, and_3_out, and_4_out, G3_out);
  Hex_Digit_Display hex_digit_display_1 (.value(S0_out));  // open: dp
  Hex_Digit_Display hex_digit_display_2 (.value({{3{in_6}}, C4_out[0]}));  // open: dp
  // Pins of 1 and 2 bits meet at S0_out[3:2]
endmodule
